// Logisim project comp1.circ as structural Verilog: 2 circuits, main circuit main
module main (
);

  wire ADD, AI, ALO, and_1_out, and_2_out, and_3_out, and_4_out, AO, BI, BO, button_1_out, CE, clk,
       clock_1_out, CO, II, IO, JMP, MI, OI, R, RI, RO, SUB, switch_1_p2, switch_2_p2, switch_3_p2;
  wire [3:0] controlled_buffer_10_out, counter_1_q, II_PIN, MAR_q, OUTPUT_REG_q, OUTPUT_REG_q_2, register_1_q;
  wire [7:0] adder_1_out, ALU_IN_A, ALU_IN_B, BUS_1, controlled_buffer_5_out, dipswitch_1_sw1, RAM_1_dout,
       subtractor_1_out;
  wire [23:16] pull_resistor_1_node;

  Pull_Resistor pull_resistor_1 (.node({pull_resistor_1_node, IO, OI, CO, JMP, CE, RO, RI, MI, II, SUB, ADD, ALO, BO, BI, AO, AI}));
  CTRL ctrl_1 (
    .CLK(clk), .R(R), .IR_IN(II_PIN),
    .CONTROL_PINS({pull_resistor_1_node, IO, OI, CO, JMP, CE, RO, RI, MI, II, SUB, ADD, ALO, BO, BI, AO, AI}));
  // Switch switch_1: pin names not known; wires that end beside it: 1'b1, switch_1_p2
  DipSwitch dipswitch_1 (
    .sw1(dipswitch_1_sw1[0]), .sw2(dipswitch_1_sw1[1]), .sw3(dipswitch_1_sw1[2]), .sw4(dipswitch_1_sw1[3]),
    .sw5(dipswitch_1_sw1[4]), .sw6(dipswitch_1_sw1[5]), .sw7(dipswitch_1_sw1[6]), .sw8(dipswitch_1_sw1[7]));
  Register A_REG (.D(BUS_1), .en(AI), .clk(clk), .Q(ALU_IN_A), .clr(R));
  Register REG_B (.D(BUS_1), .en(BI), .clk(clk), .Q(ALU_IN_B), .clr(R));
  Pull_Resistor pull_resistor_2 (.node(switch_1_p2));
  assign BUS_1 = switch_1_p2 ? dipswitch_1_sw1 : 8'bz;  // Controlled_Buffer controlled_buffer_1
  Pull_Resistor pull_resistor_3 (.node(BUS_1));
  assign BUS_1 = AO ? ALU_IN_A : 8'bz;  // Controlled_Buffer controlled_buffer_2
  assign BUS_1 = BO ? ALU_IN_B : 8'bz;  // Controlled_Buffer controlled_buffer_3
  // Switch switch_2: pin names not known; wires that end beside it: 1'b1, switch_2_p2
  Pull_Resistor pull_resistor_4 (.node(switch_2_p2));
  Pull_Resistor pull_resistor_5 (.node(BUS_1));
  assign BUS_1 = switch_2_p2 ? 8'h3 : 8'bz;  // Controlled_Buffer controlled_buffer_4
  Register OUTPUT_REG (.D(BUS_1), .en(OI), .clk(clk), .Q({OUTPUT_REG_q_2, OUTPUT_REG_q}));  // open: clr
  // Probe on BUS_1
  LedBar ledbar_1 (
    .led0(BUS_1[7]), .led1(BUS_1[6]), .led2(BUS_1[5]), .led3(BUS_1[4]), .led4(BUS_1[3]), .led5(BUS_1[2]),
    .led6(BUS_1[1]), .led7(BUS_1[0]));
  LedBar ledbar_2 (
    .led0(OUTPUT_REG_q_2[3]), .led1(OUTPUT_REG_q_2[2]), .led2(OUTPUT_REG_q_2[1]), .led3(OUTPUT_REG_q_2[0]),
    .led4(OUTPUT_REG_q[3]), .led5(OUTPUT_REG_q[2]), .led6(OUTPUT_REG_q[1]), .led7(OUTPUT_REG_q[0]));
  Register #(.width(4)) MAR (.D(BUS_1[3:0]), .en(MI), .clk(clk), .Q(MAR_q), .clr(R));
  Pull_Resistor pull_resistor_6 (.node(BUS_1));
  Hex_Digit_Display hex_digit_display_1 (.value(OUTPUT_REG_q_2));  // open: dp
  Hex_Digit_Display hex_digit_display_2 (.value(OUTPUT_REG_q));  // open: dp
  RAM #(.addrWidth(4), .asyncread("true"), .clearpin("true"), .\type ("nonvolatile")) RAM_1 (
    .addr(MAR_q), .we(RI), .oe(RO), .clk(clk), .din(controlled_buffer_5_out), .dout(RAM_1_dout));  // open: clr
  assign controlled_buffer_5_out = RI ? BUS_1 : 8'bz;  // Controlled_Buffer controlled_buffer_5
  // Switch switch_3: pin names not known; wires that end beside it: 1'b1, switch_3_p2
  Clock clock_1 (.out(clock_1_out));
  Button button_1 (.out(button_1_out));
  Button button_2 (.out(R));
  Pull_Resistor pull_resistor_7 (.node(switch_3_p2));
  and and_1 (and_1_out, switch_3_p2, clock_1_out);
  and and_2 (and_2_out, ALO, ADD, ~SUB);  // AND_Gate
  Adder adder_1 (.a(ALU_IN_A), .b(ALU_IN_B), .out(adder_1_out));  // open: cin, cout
  and and_3 (and_3_out, ALO, ~ADD, SUB);  // AND_Gate
  Subtractor subtractor_1 (.a(ALU_IN_A), .b(ALU_IN_B), .out(subtractor_1_out));  // open: bin, bout
  or or_1 (clk, and_1_out, button_1_out);
  assign BUS_1 = and_2_out ? adder_1_out : 8'bz;  // Controlled_Buffer controlled_buffer_6
  assign BUS_1 = and_3_out ? subtractor_1_out : 8'bz;  // Controlled_Buffer controlled_buffer_7
  assign BUS_1 = RO ? RAM_1_dout : 8'bz;  // Controlled_Buffer controlled_buffer_8
  Register register_1 (.D(BUS_1), .en(II), .clk(clk), .Q({II_PIN, register_1_q}), .clr(R));
  assign BUS_1 = IO ? {II_PIN, register_1_q} : 8'bz;  // Controlled_Buffer controlled_buffer_9
  and and_4 (and_4_out, CE, clk);
  assign controlled_buffer_10_out = JMP ? BUS_1[3:0] : 4'bz;  // Controlled_Buffer controlled_buffer_10
  Counter #(.max('hf), .width(4)) counter_1 (
    .clr(R), .load(JMP), .up(CE), .clk(and_4_out), .D(controlled_buffer_10_out), .Q(counter_1_q));  // open: count, carry
  assign BUS_1[3:0] = CO ? counter_1_q : 4'bz;  // Controlled_Buffer controlled_buffer_11

  // Other names for the same wires on the sheet: BUS_4LSB[3:0] = BUS_1[3:0]; BUS_4HSB[3:0] = BUS_1[7:4]
endmodule

module CTRL (
  input  CLK,
  input  R,
  input  [3:0] IR_IN,
  output [23:0] CONTROL_PINS
);

  wire and_1_out, buffer_1_out, decoder_1_out0, decoder_1_out2, decoder_1_out3, decoder_1_out4, not_1_out,
       or_1_out;
  wire [2:0] counter_1_q, counter_2_q;
  wire [23:0] dipswitch_1_p1, rom_1_data;

  Pull_Resistor pull_resistor_1 (.node(CONTROL_PINS));
  not not_1 (not_1_out, CLK);
  buf buffer_1 (buffer_1_out, R);
  // DipSwitch #(.number(16)) dipswitch_1: pin names not known; wires that end beside it: dipswitch_1_p1
  // Probe on dipswitch_1_p1
  Decoder #(.select(3)) decoder_1 (
    .out0(decoder_1_out0), .out1(CONTROL_PINS[11]), .out2(decoder_1_out2), .out3(decoder_1_out3),
    .out4(decoder_1_out4), .out5(buffer_1_out), .sel(counter_1_q));  // open: out6, out7, en
  Counter #(.max('h7), .width(3)) counter_1 (
    .count(1'b1), .Q(counter_1_q), .up(1'b1), .clk(not_1_out), .clr(buffer_1_out));  // open: load, D, carry
  and and_1 (and_1_out, or_1_out, not_1_out);
  or or_1 (or_1_out, decoder_1_out2, decoder_1_out3, decoder_1_out4);
  Counter #(.max('h7), .width(3)) counter_2 (
    .count(1'b1), .Q(counter_2_q), .up(1'b1), .clk(and_1_out), .clr(buffer_1_out));  // open: load, D, carry
  buf buffer_2 (CONTROL_PINS[8], decoder_1_out0);
  buf buffer_3 (CONTROL_PINS[13], decoder_1_out0);
  buf buffer_4 (CONTROL_PINS[10], CONTROL_PINS[11]);
  buf buffer_5 (CONTROL_PINS[7], CONTROL_PINS[11]);
  ROM #(.addrWidth(7), .dataWidth(24)) rom_1 (.addr({IR_IN, counter_2_q}), .data(rom_1_data));
  assign CONTROL_PINS = and_1_out ? rom_1_data : 24'bz;  // Controlled_Buffer controlled_buffer_1

  // Other names for the same wires on the sheet: AI = CONTROL_PINS[0]; O[23:0] = CONTROL_PINS; AO = CONTROL_PINS[1];
  //   BI = CONTROL_PINS[2]; BO = CONTROL_PINS[3]; ALO = CONTROL_PINS[4]; ADD = CONTROL_PINS[5]; SUB = CONTROL_PINS[6];
  //   II = CONTROL_PINS[7]; MI = CONTROL_PINS[8]; RI = CONTROL_PINS[9]; RO = CONTROL_PINS[10]; CE = CONTROL_PINS[11];
  //   JMP = CONTROL_PINS[12]; CO = CONTROL_PINS[13]; OI = CONTROL_PINS[14]; IO = CONTROL_PINS[15]

  // Notes on the sheet:
  //   CONTROL_PINS: pull=down
  //   buffer_1 drives only 1 and floats otherwise
  //   buffer_2 drives only 1 and floats otherwise
  //   buffer_3 drives only 1 and floats otherwise
  //   buffer_4 drives only 1 and floats otherwise
  //   buffer_5 drives only 1 and floats otherwise
  //   contents of rom_1 (hex, n*v repeats v):
  //   0 8100 401 6*0 8100 404 31 5*0 4002 7*0 8100 202
endmodule
